# Fritzing sketch CO_Clock (saved by Fritzing 1.0.2b)
stripboards: 1

parts:
  J1 = STM32 Nucleo boards
  J1_2 = Camdenboss CTB0158-4 [part_number=CTB0158-4 package=THT]
  J2 = Camdenboss CTB0158-2 [part_number=CTB0158-2 package=THT]
  C1 = Electrolytic Capacitor [capacitance=4.7µF voltage=35V package="200 mil [THT, electrolytic]"]
  R1 = Resistor [tolerance=±5% resistance=22k power=0.25W package=THT]
  R2 = Resistor [tolerance=±5% resistance=22k power=0.25W package=THT]
  R3 = Resistor [tolerance=±5% resistance=100 power=0.25W package=THT]
  Q1 = TRANSISTOR_NPN [package=to-92]
  LED1 = LED - 3mm [color="Red (633nm)" current=0.030A package="3 mm [THT]"]
  R4 = Resistor [tolerance=±5% resistance=220 power=0.25W package=THT]
  R5 = Resistor [tolerance=±5% resistance=1M power=0.25W package=THT]
  R7 = Resistor [tolerance=±5% resistance=100 power=0.25W package=THT]
  R6 = Resistor [tolerance=±5% resistance=220 power=0.25W package=THT]
  C3 = Ceramic Capacitor [capacitance=100nF voltage=35V package="100 mil [THT, multilayer]"]
  Q2 = TRANSISTOR_NPN [package=to-92]
  V1 = DC Power [voltage=12V]
  J3 = Camdenboss CTB0158-5 [part_number=CTB0158-5 package=THT]
  S1 = Pushbutton [package="[THT]"]
  S2 = Pushbutton [package="[THT]"]
  S3 = Pushbutton [package="[THT]"]
  S4 = Pushbutton [package="[THT]"]
  S5 = Pushbutton [package="[THT]"]
  C4 = Ceramic Capacitor [capacitance=100nF voltage=35V package="100 mil [THT, multilayer]"]
  R8 = Resistor [tolerance=±5% resistance=4.7k power=0.25W package=THT]
  C5 = Ceramic Capacitor [capacitance=100nF voltage=35V package="100 mil [THT, multilayer]"]
  R9 = Resistor [tolerance=±5% resistance=4.7k power=0.25W package=THT]
  C6 = Ceramic Capacitor [capacitance=100nF voltage=35V package="100 mil [THT, multilayer]"]
  C7 = Ceramic Capacitor [capacitance=100nF voltage=35V package="100 mil [THT, multilayer]"]
  C8 = Ceramic Capacitor [capacitance=100nF voltage=35V package="100 mil [THT, multilayer]"]
  R10 = Resistor [tolerance=±5% resistance=4.7k power=0.25W package=THT]
  R11 = Resistor [tolerance=±5% resistance=4.7k power=0.25W package=THT]
  R12 = Resistor [tolerance=±5% resistance=4.7k power=0.25W package=THT]
  U1 = Voltage Regulator - 5V [package="TO220 [THT]"]
  Composant1 = 4x Matrix LED 8x8 with MAX7219 [part_number=FC-16]
  Composant2 = 4x Matrix LED 8x8 with MAX7219 [part_number=FC-16]
  SPKR1 = Loudspeaker

nets:
  GND: J1.GND, J1_2.pin1, C1.-, Q1.E, R5.Pin_1, C3.1, Q2.E, V1.V-, J3.pin4, S1.Pin_3, S1.Pin_4, S2.Pin_3, S2.Pin_4, S3.Pin_3, S3.Pin_4, S4.Pin_3, S4.Pin_4, S5.Pin_3, S5.Pin_4, C4.0, C5.0, C6.0, C7.0, C8.0, U1.GND
  3V3: J1.3v3, J1.3V3, R1.Pin_0, R2.Pin_0, R4.Pin_0, R8.Pin_0, R9.Pin_0, R10.Pin_0, R11.Pin_0, R12.Pin_0
  N1: J1.D8, S5.Pin_1, S5.Pin_2, C8.1, R12.Pin_1
  N2: J1.D0/RX, S1.Pin_1, S1.Pin_2, C4.1, R8.Pin_1
  N3: J1.D1/TX, S2.Pin_1, S2.Pin_2, C5.1, R9.Pin_1
  N4: J1.D2, S3.Pin_1, S3.Pin_2, C6.1, R10.Pin_1
  N5: J1.D3_PWM, S4.Pin_1, S4.Pin_2, C7.1, R11.Pin_1
  N6: J1.D4, J1_2.pin4, R1.Pin_1
  N7: J1.D6_PWM, R5.Pin_0, R7.Pin_1
  N8: J1.D7, J3.pin2
  N9: J1.PB15, J3.pin3
  N10: J1.PB13, J3.pin1
  N11: J1.VIN, J1_2.pin2, C1.+, R6.Pin_1, V1.V+, U1.input_voltage
  N12: J1_2.pin3, R2.Pin_1, R3.Pin_0
  N13: J2.pin1, Q2.C
  N14: J2.pin2, R6.Pin_0
  N15: J2.terminal_1, SPKR1.pin1
  N16: J2.terminal_2, SPKR1.pin2
  N17: R3.Pin_1, Q1.B
  N18: Q1.C, LED1.cathode
  N19: LED1.anode, R4.Pin_1
  N20: R7.Pin_0, Q2.B
  N21: C3.0, J3.pin5, U1.output_voltage
  N22: J3.terminal_1, Composant2.CLK
  N23: J3.terminal_2, Composant2.CS
  N24: J3.terminal_3, Composant2.DIN
  N25: J3.terminal_4, Composant2.GND#1
  N26: J3.terminal_5, Composant2.VCC#0
  N27: Composant1.VCC, Composant2.VCC#5
  N28: Composant1.GND, Composant2.GND#6
  N29: Composant1.CS, Composant2.CS(OUT)
  N30: Composant1.CLK, Composant2.CLK(OUT)
  N31: Composant1.DIN, Composant2.DOUT

custom parts:
  4x Matrix LED 8x8 with MAX7219: FC-16
